// Logisim project CRC.circ as structural Verilog: 2 circuits, main circuit CRC
module CRC (
  input  [7:0] A,
  input  [3:0] B,
  output [10:0] C
);

  wire [3:1] bit3_0, bit4_1, bit5_2, bit6_3, bit7_4, bit8_5, bit9_6;
  wire [3:3] fourcrc_1_c_s, fourcrc_2_c_s, fourcrc_3_c_s, fourcrc_4_c_s, fourcrc_5_c_s, fourcrc_6_c_s,
       fourcrc_7_c_s, fourcrc_8_c_s;

  FourCRC fourcrc_1 (.A_bcs(A[7:4]), .B_cs(B), .C_s({fourcrc_1_c_s[3], bit9_6}));
  FourCRC fourcrc_2 (.A_bcs({bit7_4, A[1]}), .B_cs(B), .C_s({fourcrc_2_c_s[3], bit6_3}));
  FourCRC fourcrc_3 (.A_bcs({bit4_1, 1'b0}), .B_cs(B), .C_s({fourcrc_3_c_s[3], bit3_0}));
  FourCRC fourcrc_4 (.A_bcs({bit9_6, A[3]}), .B_cs(B), .C_s({fourcrc_4_c_s[3], bit8_5}));
  FourCRC fourcrc_5 (.A_bcs({bit6_3, A[0]}), .B_cs(B), .C_s({fourcrc_5_c_s[3], bit5_2}));
  FourCRC fourcrc_6 (.A_bcs({bit3_0, 1'b0}), .B_cs(B), .C_s({fourcrc_6_c_s[3], C[2:0]}));
  FourCRC fourcrc_7 (.A_bcs({bit8_5, A[2]}), .B_cs(B), .C_s({fourcrc_7_c_s[3], bit7_4}));
  FourCRC fourcrc_8 (.A_bcs({bit5_2, 1'b0}), .B_cs(B), .C_s({fourcrc_8_c_s[3], bit4_1}));

  assign C[10:3] = A;

  // Other names for the same wires on the sheet: bit4 = A[1]; bit7_4[0] = A[1]; inputA[7:0] = A; bit3 = A[0];
  //   bit6_3[0] = A[0]; bit5 = A[2]; bit8_5[0] = A[2]; bit6 = A[3]; bit9_6[0] = A[3]; bit10_7[3:0] = A[7:4];
  //   inputB[3:0] = B
endmodule

module FourCRC (
  input  [3:0] A_bcs,
  input  [3:0] B_cs,
  output [3:0] C_s
);

  wire [3:0] xor_1_out;

  assign xor_1_out = A_bcs ^ B_cs;  // XOR_Gate xor_1, 4 bits wide
  Multiplexer #(.width(4), .enable("false")) multiplexer_1 (.in0(A_bcs), .in1(xor_1_out), .out(C_s), .sel(A_bcs[3]));

  // Other names for the same wires on the sheet: bit3 = A_bcs[3]
endmodule
