// Logisim project FSM.circ as structural Verilog: 3 circuits, main circuit fsm
module fsm (
  input  [1:0] In,
  input  CLR,
  output Z
);

  wire clock_1_out, register_1_q, s0, s1, s2;
  wire [2:0] nextstate_1_ns0;

  Clock clock_1 (.out(clock_1_out));
  nextstate nextstate_1 (
    .s2(s2), .s1(s1), .s0(s0), .in1(In[1]), .in0(In[0]), .ns2(nextstate_1_ns0[2]), .ns1(nextstate_1_ns0[1]),
    .ns0(nextstate_1_ns0[0]));
  Register #(.width(1)) register_1 (.D(CLR), .Q(register_1_q), .clk(clock_1_out), .clr(register_1_q));  // open: en
  Register #(.width(3)) register_2 (
    .D(nextstate_1_ns0), .Q({s2, s1, s0}), .clk(clock_1_out), .clr(register_1_q));  // open: en
  \output  output_1 (.s2(s2), .s1(s1), .s0(s0), .in1(In[1]), .in0(In[0]), .z(Z));

  // Other names for the same wires on the sheet: i0 = In[0]; i1 = In[1]
endmodule

module nextstate (
  input  s2,
  input  s1,
  input  s0,
  input  in1,
  input  in0,
  output ns2,
  output ns1,
  output ns0
);

  wire and_1_out, and_2_out, and_3_out, and_4_out, and_5_out, and_6_out, and_7_out, and_8_out, not_1_out,
       not_2_out, not_3_out, not_4_out, not_5_out, not_6_out, not_7_out, not_8_out, not_9_out, not_10_out,
       not_11_out, not_12_out, not_13_out, not_14_out, not_15_out, not_16_out, not_17_out, not_18_out,
       not_19_out, not_20_out, not_21_out, not_22_out, not_23_out, not_24_out, not_25_out;

  not not_1 (not_1_out, s2);
  not not_2 (not_2_out, s1);
  not not_3 (not_3_out, in0);
  not not_4 (not_4_out, s2);
  not not_5 (not_5_out, s0);
  not not_6 (not_6_out, in0);
  not not_7 (not_7_out, s2);
  not not_8 (not_8_out, s1);
  not not_9 (not_9_out, in1);
  not not_10 (not_10_out, s2);
  not not_11 (not_11_out, s0);
  not not_12 (not_12_out, in1);
  not not_13 (not_13_out, s1);
  not not_14 (not_14_out, s0);
  not not_15 (not_15_out, in1);
  not not_16 (not_16_out, s2);
  not not_17 (not_17_out, s1);
  not not_18 (not_18_out, in1);
  not not_19 (not_19_out, in0);
  not not_20 (not_20_out, s2);
  not not_21 (not_21_out, s0);
  not not_22 (not_22_out, in1);
  not not_23 (not_23_out, in0);
  not not_24 (not_24_out, s2);
  not not_25 (not_25_out, in1);
  and and_1 (and_1_out, not_1_out, not_2_out, s0, in1, not_3_out);
  and and_2 (and_2_out, not_4_out, s1, not_5_out, in1, not_6_out);
  and and_3 (and_3_out, not_7_out, not_8_out, s0, not_9_out);
  and and_4 (and_4_out, not_10_out, s1, not_11_out, not_12_out);
  and and_5 (and_5_out, not_13_out, not_14_out, not_15_out, in0);
  and and_6 (and_6_out, not_16_out, not_17_out, s0, not_18_out, not_19_out);
  and and_7 (and_7_out, not_20_out, s1, not_21_out, not_22_out, not_23_out);
  and and_8 (and_8_out, not_24_out, s1, s0, not_25_out, in0);
  or or_1 (ns2, and_1_out, and_2_out);
  or or_2 (ns1, and_3_out, and_4_out);
  or or_3 (ns0, and_5_out, and_6_out, and_7_out, and_8_out);
endmodule

module \output  (
  input  s2,
  input  s1,
  input  s0,
  input  in1,
  input  in0,
  output z
);

  wire and_1_out, and_2_out, not_1_out, not_2_out, not_3_out, not_4_out, not_5_out;

  not not_1 (not_1_out, s2);
  not not_2 (not_2_out, in0);
  not not_3 (not_3_out, s1);
  not not_4 (not_4_out, s0);
  not not_5 (not_5_out, in0);
  and and_1 (and_1_out, not_1_out, s1, s0, not_2_out);
  and and_2 (and_2_out, s2, not_3_out, not_4_out, not_5_out);
  or or_1 (z, and_1_out, and_2_out);
endmodule
