// Logisim project GRF.circ as structural Verilog: 1 circuit, main circuit grf
module grf (
  input  clk,
  input  reset,
  input  [31:0] WD,
  input  WE,
  input  [4:0] A3,
  input  [4:0] A1,
  input  [4:0] A2,
  output [31:0] RD1,
  output [31:0] RD2
);

  wire [31:0] in0, in1, in2, in3, in4, in5, in6, in7, in8, in9, in10, in11, in12, in13, in14, in15, in16,
       in17, in18, in19, in20, in21, in22, in23, in24, in25, in26, in27, in28, in29, in30, in31, o0, o1, o2,
       o3, o4, o5, o6, o7, o8, o9, o10, o11, o12, o13, o14, o15, o16, o17, o18, o19, o20, o21, o22, o23, o24,
       o25, o26, o27, o28, o29, o30, o31;

  Demultiplexer #(.select(5), .width(32), .tristate("true")) demultiplexer_1 (
    .out0(in0), .out1(in1), .out2(in2), .out3(in3), .out4(in4), .out5(in5), .out6(in6), .out7(in7),
    .out8(in8), .out9(in9), .out10(in10), .out11(in11), .out12(in12), .out13(in13), .out14(in14),
    .out15(in15), .out16(in16), .out17(in17), .out18(in18), .out19(in19), .out20(in20), .out21(in21),
    .out22(in22), .out23(in23), .out24(in24), .out25(in25), .out26(in26), .out27(in27), .out28(in28),
    .out29(in29), .out30(in30), .out31(in31), .in(WD), .sel(A3), .en(WE));
  Register #(.width(32)) _0 (.D({32{1'b0}}), .Q(o0), .clk(clk), .clr(reset));  // open: en
  Register #(.width(32)) _1 (.D(in1), .Q(o1), .clk(clk), .clr(reset));  // open: en
  Register #(.width(32)) _2 (.D(in2), .Q(o2), .clk(clk), .clr(reset));  // open: en
  Register #(.width(32)) _3 (.D(in3), .Q(o3), .clk(clk), .clr(reset));  // open: en
  Register #(.width(32)) _4 (.D(in4), .Q(o4), .clk(clk), .clr(reset));  // open: en
  Register #(.width(32)) _5 (.D(in5), .Q(o5), .clk(clk), .clr(reset));  // open: en
  Register #(.width(32)) _6 (.D(in6), .Q(o6), .clk(clk), .clr(reset));  // open: en
  Register #(.width(32)) _7 (.D(in7), .Q(o7), .clk(clk), .clr(reset));  // open: en
  Register #(.width(32)) _8 (.D(in8), .Q(o8), .clk(clk), .clr(reset));  // open: en
  Register #(.width(32)) _9 (.D(in9), .Q(o9), .clk(clk), .clr(reset));  // open: en
  Register #(.width(32)) _10 (.D(in10), .Q(o10), .clk(clk), .clr(reset));  // open: en
  Register #(.width(32)) _11 (.D(in11), .Q(o11), .clk(clk), .clr(reset));  // open: en
  Register #(.width(32)) _12 (.D(in12), .Q(o12), .clk(clk), .clr(reset));  // open: en
  Register #(.width(32)) _13 (.D(in13), .Q(o13), .clk(clk), .clr(reset));  // open: en
  Register #(.width(32)) _14 (.D(in14), .Q(o14), .clk(clk), .clr(reset));  // open: en
  Register #(.width(32)) _15 (.D(in15), .Q(o15), .clk(clk), .clr(reset));  // open: en
  Register #(.width(32)) _16 (.D(in16), .Q(o16), .clk(clk), .clr(reset));  // open: en
  Register #(.width(32)) _17 (.D(in17), .Q(o17), .clk(clk), .clr(reset));  // open: en
  Register #(.width(32)) _18 (.D(in18), .Q(o18), .clk(clk), .clr(reset));  // open: en
  Register #(.width(32)) _19 (.D(in19), .Q(o19), .clk(clk), .clr(reset));  // open: en
  Register #(.width(32)) _20 (.D(in20), .Q(o20), .clk(clk), .clr(reset));  // open: en
  Register #(.width(32)) _21 (.D(in21), .Q(o21), .clk(clk), .clr(reset));  // open: en
  Register #(.width(32)) _22 (.D(in22), .Q(o22), .clk(clk), .clr(reset));  // open: en
  Register #(.width(32)) _23 (.D(in23), .Q(o23), .clk(clk), .clr(reset));  // open: en
  Register #(.width(32)) _24 (.D(in24), .Q(o24), .clk(clk), .clr(reset));  // open: en
  Register #(.width(32)) _25 (.D(in25), .Q(o25), .clk(clk), .clr(reset));  // open: en
  Register #(.width(32)) _26 (.D(in26), .Q(o26), .clk(clk), .clr(reset));  // open: en
  Register #(.width(32)) _27 (.D(in27), .Q(o27), .clk(clk), .clr(reset));  // open: en
  Register #(.width(32)) _28 (.D(in28), .Q(o28), .clk(clk), .clr(reset));  // open: en
  Register #(.width(32)) _29 (.D(in29), .Q(o29), .clk(clk), .clr(reset));  // open: en
  Register #(.width(32)) _30 (.D(in30), .Q(o30), .clk(clk), .clr(reset));  // open: en
  Register #(.width(32)) _31 (.D(in31), .Q(o31), .clk(clk), .clr(reset));  // open: en
  Multiplexer #(.select(5), .width(32), .enable("false")) multiplexer_1 (
    .in0(o0), .in1(o1), .in2(o2), .in3(o3), .in4(o4), .in5(o5), .in6(o6), .in7(o7), .in8(o8), .in9(o9),
    .in10(o10), .in11(o11), .in12(o12), .in13(o13), .in14(o14), .in15(o15), .in16(o16), .in17(o17),
    .in18(o18), .in19(o19), .in20(o20), .in21(o21), .in22(o22), .in23(o23), .in24(o24), .in25(o25),
    .in26(o26), .in27(o27), .in28(o28), .in29(o29), .in30(o30), .in31(o31), .out(RD1), .sel(A1));
  Multiplexer #(.select(5), .width(32), .enable("false")) multiplexer_2 (
    .in0(o0), .in1(o1), .in2(o2), .in3(o3), .in4(o4), .in5(o5), .in6(o6), .in7(o7), .in8(o8), .in9(o9),
    .in10(o10), .in11(o11), .in12(o12), .in13(o13), .in14(o14), .in15(o15), .in16(o16), .in17(o17),
    .in18(o18), .in19(o19), .in20(o20), .in21(o21), .in22(o22), .in23(o23), .in24(o24), .in25(o25),
    .in26(o26), .in27(o27), .in28(o28), .in29(o29), .in30(o30), .in31(o31), .out(RD2), .sel(A2));
endmodule
