// Logisim project navigation.circ as structural Verilog: 4 circuits, main circuit navigation
module navigation (
  input  [1:0] dir,
  input  clk,
  input  reset,
  output arrive,
  output hit
);

  wire hit_1_hit, ns0, ns1, ns2;
  wire [2:0] prestate;

  nextstate nextstate_1 (
    .st2(prestate[2]), .st1(prestate[1]), .ns2(ns2), .st0(prestate[0]), .dir1(dir[1]), .dir0(dir[0]),
    .ns1(ns1), .ns0(ns0));
  Register #(.width(3)) register_1 (.D({ns2, ns1, ns0}), .Q(prestate), .clk(clk), .clr(reset));  // open: en
  arrive arrive_1 (.s2(prestate[2]), .s1(prestate[1]), .s0(prestate[0]), .arrive(arrive));
  hit hit_1 (.st2(prestate[2]), .st1(prestate[1]), .st0(prestate[0]), .ns2(ns2), .ns1(ns1), .ns0(ns0), .hit(hit_1_hit));
  Register #(.width(1)) register_2 (.D(hit_1_hit), .Q(hit), .clk(clk), .clr(reset));  // open: en

  // Other names for the same wires on the sheet: st0 = prestate[0]; st1 = prestate[1]; st2 = prestate[2]
endmodule

module nextstate (
  input  st2,
  input  st1,
  input  st0,
  input  dir1,
  input  dir0,
  output ns2,
  output ns1,
  output ns0
);

  wire and_1_out, and_2_out, and_3_out, and_4_out, and_5_out, and_6_out, and_7_out, and_8_out, and_9_out,
       and_10_out, and_11_out, not_1_out, not_2_out, not_3_out, not_4_out, not_5_out, not_6_out, not_7_out,
       not_8_out, not_9_out, not_10_out, not_11_out, not_12_out, not_13_out, not_14_out, not_15_out,
       not_16_out, not_17_out, not_18_out, not_19_out, not_20_out, not_21_out, not_22_out, not_23_out,
       not_24_out, not_25_out, not_26_out, not_27_out;

  not not_1 (not_1_out, st2);
  not not_2 (not_2_out, st0);
  not not_3 (not_3_out, dir1);
  not not_4 (not_4_out, dir0);
  not not_5 (not_5_out, st2);
  not not_6 (not_6_out, dir1);
  not not_7 (not_7_out, st2);
  not not_8 (not_8_out, st1);
  not not_9 (not_9_out, dir1);
  not not_10 (not_10_out, st2);
  not not_11 (not_11_out, dir1);
  not not_12 (not_12_out, dir0);
  not not_13 (not_13_out, st2);
  not not_14 (not_14_out, st0);
  not not_15 (not_15_out, dir1);
  not not_16 (not_16_out, st2);
  not not_17 (not_17_out, st0);
  not not_18 (not_18_out, dir0);
  not not_19 (not_19_out, st2);
  not not_20 (not_20_out, st2);
  not not_21 (not_21_out, st1);
  not not_22 (not_22_out, dir1);
  not not_23 (not_23_out, dir0);
  not not_24 (not_24_out, st2);
  not not_25 (not_25_out, st2);
  not not_26 (not_26_out, st2);
  not not_27 (not_27_out, dir0);
  and and_1 (and_1_out, not_1_out, st1, not_2_out, not_3_out, not_4_out);
  and and_2 (and_2_out, not_5_out, st1, st0, not_6_out, dir0);
  and and_3 (and_3_out, not_7_out, not_8_out, st0, not_9_out);
  and and_4 (and_4_out, not_10_out, st0, not_11_out, not_12_out);
  and and_5 (and_5_out, not_13_out, st1, not_14_out, not_15_out, dir0);
  and and_6 (and_6_out, not_16_out, st1, not_17_out, dir1, not_18_out);
  and and_7 (and_7_out, not_19_out, st1, st0, dir1, dir0);
  and and_8 (and_8_out, not_20_out, not_21_out, not_22_out, not_23_out);
  and and_9 (and_9_out, not_24_out, st0, dir1, dir0);
  and and_10 (and_10_out, not_25_out, st1, dir1, dir0);
  and and_11 (and_11_out, not_26_out, st1, st0, not_27_out);
  or or_1 (ns2, and_1_out, and_2_out);
  or or_2 (ns1, and_3_out, and_4_out, and_5_out, and_6_out, and_7_out);
  or or_3 (ns0, and_8_out, and_9_out, and_10_out, and_11_out);
endmodule

module arrive (
  input  s2,
  input  s1,
  input  s0,
  output arrive
);

  wire not_1_out, not_2_out;

  not not_1 (not_1_out, s1);
  not not_2 (not_2_out, s0);
  and and_1 (arrive, s2, not_1_out, not_2_out);
endmodule

module hit (
  input  st2,
  input  st1,
  input  st0,
  input  ns2,
  input  ns1,
  input  ns0,
  output hit
);

  wire and_1_out, and_2_out, and_3_out, and_4_out, not_1_out, not_2_out, not_3_out, not_4_out, not_5_out,
       not_6_out, not_7_out, not_8_out, not_9_out, not_10_out, not_11_out, not_12_out, not_13_out,
       not_14_out, not_15_out, not_16_out;

  not not_1 (not_1_out, st2);
  not not_2 (not_2_out, st1);
  not not_3 (not_3_out, st0);
  not not_4 (not_4_out, ns2);
  not not_5 (not_5_out, ns1);
  not not_6 (not_6_out, ns0);
  not not_7 (not_7_out, st2);
  not not_8 (not_8_out, st1);
  not not_9 (not_9_out, ns2);
  not not_10 (not_10_out, ns1);
  not not_11 (not_11_out, st2);
  not not_12 (not_12_out, st0);
  not not_13 (not_13_out, ns2);
  not not_14 (not_14_out, ns0);
  not not_15 (not_15_out, st2);
  not not_16 (not_16_out, ns2);
  and and_1 (and_1_out, not_1_out, not_2_out, not_3_out, not_4_out, not_5_out, not_6_out);
  and and_2 (and_2_out, not_7_out, not_8_out, st0, not_9_out, not_10_out, ns0);
  and and_3 (and_3_out, not_11_out, st1, not_12_out, not_13_out, ns1, not_14_out);
  and and_4 (and_4_out, not_15_out, st1, st0, not_16_out, ns1, ns0);
  or or_1 (hit, and_1_out, and_2_out, and_3_out, and_4_out);
endmodule
