// Logisim project Single-circle CPU.circ as structural Verilog
module main (
  input  Reset,
  output [31:0] Instr,
  output RegWrite,
  output [4:0] RegAddr,
  output [31:0] RegData,
  output MemWrite,
  output [4:0] MemAddr,
  output [31:0] MemData
);

  wire Br, BSel, Clk, EXTOP, Memoryout;
  wire [1:0] WDSel, WRSel;
  wire [2:0] ALUOP;
  wire [31:0] alu_1_out, DM_memoryout_2, ext_1_ext, GRF_rd1, multiplexer_2_out, NPC_npc, PC_4, PC_q, ZERO;
  wire [31:5] shifter_1_out;

  Clock u_Clk (.out(Clk));
  NPC NPC (.PC(PC_q), .imm(Instr[15:0]), .Br(Br), .ZERO(ZERO), .NPC(NPC_npc), .PC_4_real(PC_4));
  Register #(.width(32)) PC (.D(NPC_npc), .Q(PC_q), .clk(Clk), .clr(Reset));  // open: en
  // Probe on Instr[31:26]
  ROM #(.addrWidth(5), .dataWidth(32)) rom_1 (.addr(PC_q[4:0]), .data(Instr));  // open: sel
  // Probe on Instr[15:0]
  // Probe on Instr[5:0]
  Multiplexer #(.select(2), .width(5)) multiplexer_1 (
    .in0(Instr[20:16]), .in1(Instr[15:11]), .out(RegAddr), .sel(WRSel));  // open: in2, in3, en
  // Probe on RegAddr
  Controller Controller (
    .op0(Instr[0]), .op1(Instr[1]), .op2(Instr[2]), .op3(Instr[3]), .op4(Instr[4]), .op5(Instr[5]),
    .op26(Instr[26]), .op27(Instr[27]), .op28(Instr[28]), .op29(Instr[29]), .op30(Instr[30]),
    .op31(Instr[31]), .RFwr(RegWrite), .WRSel(WRSel), .BSel(BSel), .EXTOP(EXTOP), .WDSel(WDSel),
    .Memoryout(Memoryout), .DMWr(MemWrite), .ALUOP(ALUOP), .Br(Br));
  EXT ext_1 (.imm16(Instr[15:0]), .EXTOP(EXTOP), .EXT(ext_1_ext));
  // Probe on ALUOP
  GRF GRF (
    .CLK(Clk), .WD(RegData), .RFWr(RegWrite), .reset(Reset), .RD1(GRF_rd1), .RD2(MemData), .RegAddr(RegAddr),
    .A1(Instr[25:21]), .A2(Instr[20:16]));
  Multiplexer #(.width(32)) multiplexer_2 (
    .in0(MemData), .in1(ext_1_ext), .out(multiplexer_2_out), .sel(BSel));  // open: en
  Multiplexer #(.select(2), .width(32)) multiplexer_3 (
    .in0(alu_1_out), .in1(DM_memoryout_2), .out(RegData), .sel(WDSel));  // open: in2, in3, en
  ALU alu_1 (.RD2(multiplexer_2_out), .OUT(alu_1_out), .RD1(GRF_rd1), .ZERO(ZERO), .ALUOP(ALUOP));
  // Probe on alu_1_out
  Shifter #(.width(32), .shift("lr")) shifter_1 (.in(alu_1_out), .\dist (5'b00010), .out({shifter_1_out, MemAddr}));
  DM DM (
    .Address(MemAddr), .WD(MemData), .Memoryout_2(DM_memoryout_2), .DMWr(MemWrite), .CLK(Clk),
    .Memoryout(Memoryout), .RESET(Reset));

  // Other names for the same wires on the sheet: DMWr = MemWrite; func[5:0] = Instr[5:0];
  //   imm_or_offset[15:0] = Instr[15:0]; index[25:0] = Instr[25:0]; rd[4:0] = Instr[15:11]; rt[4:0] = Instr[20:16];
  //   rs[4:0] = Instr[25:21]; opcode[5:0] = Instr[31:26]; RedData[31:0] = RegData; RFwr = RegWrite

  // Notes on the sheet:
  //   PC字寻址，这里的PC是指第几个指令
  //   PC
  //   imm
  //   contents of rom_1 (hex, n*v repeats v):
  //   3404007b 348501c8 3c06007b 3c07ffff 34e7ffff 868020 878820 e79020 34080000 ad040000 ad050004
  //   ad060008 ad07000c ad100010 ad110014 ad120018 8d040000 8d05000c ad04001c ad050020 34040001 34050002
  //   34060001 10850001 10860001 ad040024 ad050028
endmodule

module IFU (
  input  Clk,
  input  RESET,
  input  [15:0] imm,
  input  Br,
  input  [31:0] ZERO,
  output [31:0] code
);

  wire [31:0] NPC_npc, PC_q;

  Register #(.width(32)) PC (.D(NPC_npc), .Q(PC_q), .clk(Clk), .clr(RESET));  // open: en
  NPC NPC (.PC(PC_q), .imm(imm), .Br(Br), .ZERO(ZERO), .NPC(NPC_npc));  // open: PC_4_real
  ROM #(.addrWidth(5), .dataWidth(32)) rom_1 (.addr(PC_q[4:0]), .data(code));  // open: sel

  // Notes on the sheet:
  //   PC
  //   imm
  //   contents of rom_1 (hex, n*v repeats v):
  //   3404007b 348501c8 3c06007b 3c07ffff 34e7ffff 868020 878820 e79020 34080000 ad040000 ad050004
  //   ad060008 ad07000c ad100010 ad110014 ad120018 8d040000 8d05000c ad04001c ad050020 34040001 34050002
  //   34060001 10850001 10860001 ad040024 ad050028
endmodule

module GRF (
  input  reset,
  input  CLK,
  input  [31:0] WD,
  input  [4:0] A1,
  input  [4:0] A2,
  input  RFWr,
  input  [4:0] RegAddr,
  output [31:0] RD1,
  output [31:0] RD2
);

  wire [31:0] _0_q, _1_q, _2_q, _3_q, _4_q, _5_q, _6_q, _7_q, _8_q, _9_q, _10_q, _11_q, _12_q, _13_q, _14_q,
       _15_q, _16_q, _17_q, _18_q, _19_q, _20_q, _21_q, _22_q, _23_q, _24_q, _25_q, _26_q, _27_q, _28_q,
       _29_q, _30_q, _31_q, demultiplexer_1_out1, demultiplexer_1_out2, demultiplexer_1_out3,
       demultiplexer_1_out4, demultiplexer_1_out5, demultiplexer_1_out6, demultiplexer_1_out7,
       demultiplexer_1_out8, demultiplexer_1_out9, demultiplexer_1_out10, demultiplexer_1_out11,
       demultiplexer_1_out12, demultiplexer_1_out13, demultiplexer_1_out14, demultiplexer_1_out15,
       demultiplexer_1_out16, demultiplexer_1_out17, demultiplexer_1_out18, demultiplexer_1_out19,
       demultiplexer_1_out20, demultiplexer_1_out21, demultiplexer_1_out22, demultiplexer_1_out23,
       demultiplexer_1_out24, demultiplexer_1_out25, demultiplexer_1_out26, demultiplexer_1_out27,
       demultiplexer_1_out28, demultiplexer_1_out29, demultiplexer_1_out30, demultiplexer_1_out31;

  Demultiplexer #(.select(5), .width(32), .tristate("true")) demultiplexer_1 (
    .out1(demultiplexer_1_out1), .out2(demultiplexer_1_out2), .out3(demultiplexer_1_out3),
    .out4(demultiplexer_1_out4), .out5(demultiplexer_1_out5), .out6(demultiplexer_1_out6),
    .out7(demultiplexer_1_out7), .out8(demultiplexer_1_out8), .out9(demultiplexer_1_out9),
    .out10(demultiplexer_1_out10), .out11(demultiplexer_1_out11), .out12(demultiplexer_1_out12),
    .out13(demultiplexer_1_out13), .out14(demultiplexer_1_out14), .out15(demultiplexer_1_out15),
    .out16(demultiplexer_1_out16), .out17(demultiplexer_1_out17), .out18(demultiplexer_1_out18),
    .out19(demultiplexer_1_out19), .out20(demultiplexer_1_out20), .out21(demultiplexer_1_out21),
    .out22(demultiplexer_1_out22), .out23(demultiplexer_1_out23), .out24(demultiplexer_1_out24),
    .out25(demultiplexer_1_out25), .out26(demultiplexer_1_out26), .out27(demultiplexer_1_out27),
    .out28(demultiplexer_1_out28), .out29(demultiplexer_1_out29), .out30(demultiplexer_1_out30),
    .out31(demultiplexer_1_out31), .in(WD), .sel(RegAddr), .en(RFWr));  // open: out0
  Register #(.width(32)) _0 (.D({32{1'b0}}), .Q(_0_q), .clk(CLK), .clr(reset));  // open: en
  Register #(.width(32)) _4 (.D(demultiplexer_1_out4), .Q(_4_q), .clk(CLK), .clr(reset));  // open: en
  Register #(.width(32)) _8 (.D(demultiplexer_1_out8), .Q(_8_q), .clk(CLK), .clr(reset));  // open: en
  Register #(.width(32)) _12 (.D(demultiplexer_1_out12), .Q(_12_q), .clk(CLK), .clr(reset));  // open: en
  Register #(.width(32)) _16 (.D(demultiplexer_1_out16), .Q(_16_q), .clk(CLK), .clr(reset));  // open: en
  Register #(.width(32)) _20 (.D(demultiplexer_1_out20), .Q(_20_q), .clk(CLK), .clr(reset));  // open: en
  Register #(.width(32)) _24 (.D(demultiplexer_1_out24), .Q(_24_q), .clk(CLK), .clr(reset));  // open: en
  Register #(.width(32)) _28 (.D(demultiplexer_1_out28), .Q(_28_q), .clk(CLK), .clr(reset));  // open: en
  Register #(.width(32)) _1 (.D(demultiplexer_1_out1), .Q(_1_q), .clk(CLK), .clr(reset));  // open: en
  Register #(.width(32)) _5 (.D(demultiplexer_1_out5), .Q(_5_q), .clk(CLK), .clr(reset));  // open: en
  Register #(.width(32)) _9 (.D(demultiplexer_1_out9), .Q(_9_q), .clk(CLK), .clr(reset));  // open: en
  Register #(.width(32)) _13 (.D(demultiplexer_1_out13), .Q(_13_q), .clk(CLK), .clr(reset));  // open: en
  Register #(.width(32)) _17 (.D(demultiplexer_1_out17), .Q(_17_q), .clk(CLK), .clr(reset));  // open: en
  Register #(.width(32)) _21 (.D(demultiplexer_1_out21), .Q(_21_q), .clk(CLK), .clr(reset));  // open: en
  Register #(.width(32)) _25 (.D(demultiplexer_1_out25), .Q(_25_q), .clk(CLK), .clr(reset));  // open: en
  Register #(.width(32)) _29 (.D(demultiplexer_1_out29), .Q(_29_q), .clk(CLK), .clr(reset));  // open: en
  Register #(.width(32)) _2 (.D(demultiplexer_1_out2), .Q(_2_q), .clk(CLK), .clr(reset));  // open: en
  Register #(.width(32)) _6 (.D(demultiplexer_1_out6), .Q(_6_q), .clk(CLK), .clr(reset));  // open: en
  Register #(.width(32)) _10 (.D(demultiplexer_1_out10), .Q(_10_q), .clk(CLK), .clr(reset));  // open: en
  Register #(.width(32)) _14 (.D(demultiplexer_1_out14), .Q(_14_q), .clk(CLK), .clr(reset));  // open: en
  Register #(.width(32)) _18 (.D(demultiplexer_1_out18), .Q(_18_q), .clk(CLK), .clr(reset));  // open: en
  Register #(.width(32)) _22 (.D(demultiplexer_1_out22), .Q(_22_q), .clk(CLK), .clr(reset));  // open: en
  Register #(.width(32)) _26 (.D(demultiplexer_1_out26), .Q(_26_q), .clk(CLK), .clr(reset));  // open: en
  Register #(.width(32)) _30 (.D(demultiplexer_1_out30), .Q(_30_q), .clk(CLK), .clr(reset));  // open: en
  Register #(.width(32)) _3 (.D(demultiplexer_1_out3), .Q(_3_q), .clk(CLK), .clr(reset));  // open: en
  Register #(.width(32)) _7 (.D(demultiplexer_1_out7), .Q(_7_q), .clk(CLK), .clr(reset));  // open: en
  Register #(.width(32)) _11 (.D(demultiplexer_1_out11), .Q(_11_q), .clk(CLK), .clr(reset));  // open: en
  Register #(.width(32)) _15 (.D(demultiplexer_1_out15), .Q(_15_q), .clk(CLK), .clr(reset));  // open: en
  Register #(.width(32)) _19 (.D(demultiplexer_1_out19), .Q(_19_q), .clk(CLK), .clr(reset));  // open: en
  Register #(.width(32)) _23 (.D(demultiplexer_1_out23), .Q(_23_q), .clk(CLK), .clr(reset));  // open: en
  Register #(.width(32)) _27 (.D(demultiplexer_1_out27), .Q(_27_q), .clk(CLK), .clr(reset));  // open: en
  Register #(.width(32)) _31 (.D(demultiplexer_1_out31), .Q(_31_q), .clk(CLK), .clr(reset));  // open: en
  Multiplexer #(.select(5), .width(32)) multiplexer_1 (
    .in0(_0_q), .in1(_1_q), .in2(_2_q), .in3(_3_q), .in4(_4_q), .in5(_5_q), .in6(_6_q), .in7(_7_q),
    .in8(_8_q), .in9(_9_q), .in10(_10_q), .in11(_11_q), .in12(_12_q), .in13(_13_q), .in14(_14_q),
    .in15(_15_q), .in16(_16_q), .in17(_17_q), .in18(_18_q), .in19(_19_q), .in20(_20_q), .in21(_21_q),
    .in22(_22_q), .in23(_23_q), .in24(_24_q), .in25(_25_q), .in26(_26_q), .in27(_27_q), .in28(_28_q),
    .in29(_29_q), .in30(_30_q), .in31(_31_q), .out(RD1), .sel(A1));  // open: en
  Multiplexer #(.select(5), .width(32)) multiplexer_2 (
    .in0(_0_q), .in1(_1_q), .in2(_2_q), .in3(_3_q), .in4(_4_q), .in5(_5_q), .in6(_6_q), .in7(_7_q),
    .in8(_8_q), .in9(_9_q), .in10(_10_q), .in11(_11_q), .in12(_12_q), .in13(_13_q), .in14(_14_q),
    .in15(_15_q), .in16(_16_q), .in17(_17_q), .in18(_18_q), .in19(_19_q), .in20(_20_q), .in21(_21_q),
    .in22(_22_q), .in23(_23_q), .in24(_24_q), .in25(_25_q), .in26(_26_q), .in27(_27_q), .in28(_28_q),
    .in29(_29_q), .in30(_30_q), .in31(_31_q), .out(RD2), .sel(A2));  // open: en
endmodule

module ALU (
  input  [31:0] RD1,
  input  [31:0] RD2,
  input  [2:0] ALUOP,
  output [31:0] ZERO,
  output [31:0] OUT
);

  wire [31:0] adder_1_out, or_out, subtractor_1_out;

  Adder #(.width(32)) adder_1 (.a(RD1), .b(RD2), .out(adder_1_out));  // open: cin, cout
  Subtractor #(.width(32)) subtractor_1 (.a(RD1), .b(RD2), .out(subtractor_1_out));  // open: bin, bout
  assign or_out = RD1 | RD2;  // OR_Gate or, 32 bits wide
  assign ZERO = ~subtractor_1_out;  // NOT_Gate not_1, 32 bits wide
  Multiplexer #(.select(3), .width(32)) multiplexer_1 (
    .in0(adder_1_out), .in1(subtractor_1_out), .in2(or_out), .in3({RD2[15:0], {16{1'b0}}}), .out(OUT),
    .sel(ALUOP));  // open: in4, in5, in6, in7, en
endmodule

module DM (
  input  [4:0] Address,
  input  [31:0] WD,
  input  DMWr,
  input  CLK,
  input  Memoryout,
  input  RESET,
  output [31:0] Memoryout_2
);

  RAM #(.addrWidth(5), .dataWidth(32), .bus("separate")) ram_1 (
    .addr(Address), .din(WD), .data(Memoryout_2), .str(DMWr), .clk(CLK), .ld(Memoryout), .clr(RESET));  // open: sel
endmodule

module EXT (
  input  EXTOP,
  input  [15:0] imm16,
  output [31:0] EXT
);

  wire multiplexer_1_out;

  Multiplexer multiplexer_1 (.in0(imm16[15]), .in1(1'b0), .out(multiplexer_1_out), .sel(EXTOP));  // open: en
  assign EXT = {{16{multiplexer_1_out}}, imm16};  // Bit_Extender bit_extender_1

  // Other names for the same wires on the sheet: high = imm16[15]
endmodule

module NPC (
  input  [31:0] PC,
  input  [15:0] imm,
  input  Br,
  input  [31:0] ZERO,
  output [31:0] PC_4_real,
  output [31:0] NPC
);

  wire comparator_1_eq;
  wire [31:0] adder_1_out, adder_2_out, beq_out, bit_extender_1_out, bit_extender_2_out;

  assign bit_extender_1_out = {{16{imm[15]}}, imm};  // Bit_Extender bit_extender_1
  assign bit_extender_2_out = {{31{1'b1}}, Br};  // Bit_Extender bit_extender_2
  Adder #(.width(32)) adder_1 (.a(32'h1), .b(PC), .out(adder_1_out));  // open: cin, cout
  assign beq_out = bit_extender_2_out & ZERO;  // AND_Gate beq, 32 bits wide
  Adder #(.width(32)) adder_2 (.a(adder_1_out), .b(bit_extender_1_out), .out(adder_2_out));  // open: cin, cout
  Comparator #(.width(32), .mode("unsigned")) comparator_1 (
    .a({32{1'b1}}), .b(beq_out), .eq(comparator_1_eq));  // open: gt, lt
  Shifter #(.width(32)) shifter_1 (.in(adder_1_out), .\dist (5'b00010), .out(PC_4_real));
  Multiplexer #(.width(32)) multiplexer_1 (
    .in0(adder_1_out), .in1(adder_2_out), .out(NPC), .sel(comparator_1_eq));  // open: en
endmodule

module Controller (
  input  op0,
  input  op1,
  input  op2,
  input  op3,
  input  op4,
  input  op5,
  input  op26,
  input  op27,
  input  op28,
  input  op29,
  input  op30,
  input  op31,
  output DMWr,
  output RFwr,
  output BSel,
  output EXTOP,
  output [1:0] WDSel,
  output Memoryout,
  output [1:0] WRSel,
  output [2:0] ALUOP,
  output Br
);

  wire ADD, LUI, not_1_out, not_2_out, not_3_out, not_4_out, not_5_out, not_6_out, not_7_out, not_8_out,
       not_9_out, not_10_out, not_11_out, not_12_out, not_13_out, not_14_out, not_15_out, not_16_out,
       not_17_out, not_18_out, not_19_out, not_20_out, not_21_out, not_22_out, not_23_out, not_24_out,
       not_25_out, not_26_out, not_27_out, not_28_out, not_29_out, not_30_out, not_31_out, not_32_out,
       not_33_out, not_34_out, not_35_out, not_36_out, ORI, SUB;

  not not_1 (not_1_out, op31);
  not not_2 (not_2_out, op30);
  not not_3 (not_3_out, op29);
  not not_4 (not_4_out, op28);
  not not_5 (not_5_out, op27);
  not not_6 (not_6_out, op26);
  not not_7 (not_7_out, op4);
  not not_8 (not_8_out, op3);
  not not_9 (not_9_out, op2);
  not not_10 (not_10_out, op1);
  not not_11 (not_11_out, op0);
  not not_12 (not_12_out, op31);
  not not_13 (not_13_out, op30);
  not not_14 (not_14_out, op29);
  not not_15 (not_15_out, op28);
  not not_16 (not_16_out, op27);
  not not_17 (not_17_out, op26);
  not not_18 (not_18_out, op4);
  not not_19 (not_19_out, op3);
  not not_20 (not_20_out, op2);
  not not_21 (not_21_out, op0);
  not not_22 (not_22_out, op31);
  not not_23 (not_23_out, op30);
  not not_24 (not_24_out, op27);
  not not_25 (not_25_out, op30);
  not not_26 (not_26_out, op29);
  not not_27 (not_27_out, op28);
  not not_28 (not_28_out, op30);
  not not_29 (not_29_out, op28);
  not not_30 (not_30_out, op31);
  not not_31 (not_31_out, op30);
  not not_32 (not_32_out, op29);
  not not_33 (not_33_out, op27);
  not not_34 (not_34_out, op26);
  not not_35 (not_35_out, op31);
  not not_36 (not_36_out, op30);
  and and_1 (ADD, not_1_out, not_2_out, not_3_out, not_4_out, not_5_out, not_6_out, op5, not_7_out, not_8_out, not_9_out, not_10_out, not_11_out);
  and and_2 (SUB, not_12_out, not_13_out, not_14_out, not_15_out, not_16_out, not_17_out, op5, not_18_out, not_19_out, not_20_out, op1, not_21_out);
  and and_3 (ORI, not_22_out, not_23_out, op29, op28, not_24_out, op26);
  and and_4 (Memoryout, op31, not_25_out, not_26_out, not_27_out, op27, op26);
  and and_5 (DMWr, op31, not_28_out, op29, not_29_out, op27, op26);
  and and_6 (Br, not_30_out, not_31_out, not_32_out, op28, not_33_out, not_34_out);
  and and_7 (LUI, not_35_out, not_36_out, op29, op28, op27, op26);
  or u_RFwr (RFwr, ADD, SUB, ORI, Memoryout, LUI);
  or WRSel1 (WRSel[1], 1'b0, 1'b0);
  or WRSel0 (WRSel[0], ADD, SUB);
  or u_BSel (BSel, ORI, Memoryout, DMWr, LUI);
  or u_EXTOP (EXTOP, ORI, DMWr);
  or ALUOP2 (ALUOP[2], 1'b0, 1'b0);
  or ALUOP1 (ALUOP[1], ORI, LUI);
  or ALUOP0 (ALUOP[0], SUB, Br, LUI);

  assign WDSel = {1'b0, Memoryout};

  // Other names for the same wires on the sheet: BEQ = Br; SW = DMWr; LW = Memoryout
endmodule
